# Fritzing sketch SMD_RGB_RPi4B (saved by Fritzing 0.8.7b)
breadboards: 1

parts:
  Mod1 = Raspberry Pi 4B
  Part1 = KY-009 Full Color RGB LED SMD Module [package="Breakout board"]

nets:
  N1: Mod1.GPIO13, Part1.G
  N2: Mod1.GPIO19, Part1.R
  N3: Mod1.GPIO26, Part1.B
  N4: Mod1.GND, Part1.-

custom parts:
  KY-009 Full Color RGB LED SMD Module: RGB full color LED Module KY-009 for Arduino, emits a range of colors by mixing red, green and blue. The amount of each primary color is adjusted using PWM.
